# Fritzing sketch schematics (saved by Fritzing 0.9.3b)

parts:
  U1 = atmega168 [package=dip]
  Part1 = HX711 Weighing Sensor Module
  LED1 = 7-SEGMENT-4DIGIT-YOUNGSUN [package=7-segment-4digit-youngsun-longpads]
  R1 = Resistor [tolerance=±5% resistance=330 package="1206 [SMD]"]
  R2 = Resistor [tolerance=±5% resistance=330 package="1206 [SMD]"]
  R3 = Resistor [tolerance=±5% resistance=330 package="1206 [SMD]"]
  R4 = Resistor [tolerance=±5% resistance=330 package="1206 [SMD]"]
  JP1 = Header 4 [package=1x04-smd]
  JP2 = Header 2 [package=jst-2-pth]
  S1 = Momentary Switch [package=tactile-pth]
  R5 = Resistor [tolerance=±5% resistance=10k package="1206 [SMD]"]
  Part2 = NRF24L01+ Breakout Board
  BAT1 = Battery Holders [package=battcon_12mm]

nets:
  N1: U1.RESET, S1.4
  N2: U1.D0_(RX), JP2.1
  N3: U1.D1_(TX), JP2.2
  N4: U1.D3_(PWM), LED1.G
  N5: U1.D4, LED1.C
  3.3V: U1.VCC, U1.AVCC, Part1.VCC, R5.Pin_1, Part2.VCC, BAT1.+
  GND: U1.GND, Part1.GND, S1.2, Part2.GND, BAT1.-
  N6: U1.XLAT1, LED1.DP
  N7: U1.XLAT2, LED1.D
  N8: U1.D5_(PWM), LED1.E
  N9: U1.D6_(PWM), Part1.CK/TX
  N10: U1.D7, Part1.DO/RX
  N11: U1.D8, R3.Pin_0
  N12: U1.D9_(PWM), Part2.CE
  N13: U1.D10_(PWM), Part2.CS
  N14: U1.D11_(PWM), Part2.MOSI
  N15: U1.D12, Part2.MISO
  N16: U1.D13, Part2.SCK
  N17: U1.A0, R2.Pin_1
  N18: U1.A1, LED1.A
  N19: U1.A2, LED1.F
  N20: U1.A3, R1.Pin_1
  N21: U1.A4, R4.Pin_1
  N22: U1.A5, LED1.B
  N23: Part1.E+, JP1.4
  N24: Part1.E-, JP1.3
  N25: Part1.A+, JP1.1
  N26: Part1.A-, JP1.2
  N27: LED1.DIG1, R2.Pin_0
  N28: LED1.DIG2, R1.Pin_0
  N29: LED1.DIG3, R4.Pin_0
  N30: LED1.DIG4, R3.Pin_1
  N31: S1.3, R5.Pin_0

notes:
  serial
  to the wheatstone bridge of load cells
  Power on (reset) switch
